# Fritzing sketch laser-tof-VL53L1X-reading (saved by Fritzing 0.9.3b)
breadboards: 1

parts:
  Part2 = Adafruit VL53L0X Time of Flight Distance Sensor [part_number="Adafruit #3317"]
  Part4 = Genuino 101

nets:
  VIN: Part2.VIN, Part4.5V
  GND: Part2.GND, Part4.GND
  N1: Part2.SCL, Part4.A5/SCL
  N2: Part2.SDA, Part4.A4/SDA

notes:
  VIN = 3-6V
  (Couldn't find exact version of VL531X)

custom parts:
  Adafruit VL53L0X Time of Flight Distance Sensor: The VL53L0X is a Time of Flight distance sensor like no other you've used! The sensor contains a very tiny invisible laser source, and a matching sensor. The VL53L0X can detect the "time of flight", or how long the light has taken to bounce back to the sensor. Since it uses a very narrow light source, it is good for determining distance of only the surface directly in front of it. Unlike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
  Genuino 101: A learning and development board that delivers the performance and low-power consumption of the Intel® Curie™ Module with the simplicity of Arduino at an entry-level price. It keeps the same robust form factor and peripheral list of the UNO with the addition of onboard Bluetooth LE capabilities and a 6-axis accelerometer/gyro to help you easily expand your creativity into the connected world.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
